# Fritzing sketch Car LED Controller (saved by Fritzing 0.9.10b)
breadboards: 3

parts:
  Part4 = TXB0108 8-channel Bi-directional Logic Level Converter  # not connected
  JP1 = Header 4 [package=molex-1x4_lock]  # not connected
  J1 = shrouded pin header, 16 pins [form="♂ (shrouded male)"]  # not connected
  J3 = Camdenboss CTB0158-2 [part_number=CTB0158-2 package=THT]  # not connected
  Part3 = TXB0108 8-channel Bi-directional Logic Level Converter  # not connected
  Power_plug1 = Power plug
  U6 = SK6812 RGBW LED Strip
  R16 = Resistor [tolerance=±5% power=0.25 resistance=1M package=THT]
  Part2 = LCD1602-I2C
  Part1 = Logic Level Converter
  J2 = Camdenboss CTB0158-4 [part_number=CTB0158-4 package=THT]
  R12 = Resistor [tolerance=±5% power=0.25 resistance=47k package=THT]
  C2 = Capacitor [package=cap-pth-small2]
  R18 = Resistor [tolerance=±5% power=0.25 resistance=1M package=THT]
  MH-ET_LIVE_ESP32_DEVKIT1 = MH-ET LIVE ESP32 DEVKIT 38 pins
  M2 = RioRand LM2596
  M1 = RioRand LM2596
  R13 = Resistor [tolerance=±5% power=0.25 resistance=47k package=THT]
  C3 = Capacitor [package=cap-pth-small2]
  U7 = 2-Channel 5v Relay Shield [package=relay-2ch5v10a]
  R17 = Resistor [tolerance=±5% power=0.25 resistance=1M package=THT]
  C1 = Capacitor [package=cap-pth-small2]
  R11 = Resistor [tolerance=±5% power=0.25 resistance=1M package=THT]
  R15 = Resistor [tolerance=±5% power=0.25 resistance=1M package=THT]
  S2 = Momentary Switch [package=ksa_sealed_tac_switch]
  R14 = Resistor [tolerance=±5% power=0.25 resistance=47k package=THT]
  C4 = Capacitor [package=cap-pth-small2]

nets:
  N1: Power_plug1.VCC, M2.Pin_1, M1.Pin_1
  N2: Power_plug1.GND, M2.Pin_2, M1.Pin_2
  GND: U6.GND#0, R16.Pin_0, Part2.GND, Part1.TX2_LV, Part1.GND, J2.pin4, R12.Pin_0, C2.1, C2.2, R18.Pin_0, R18.Pin_1, MH-ET_LIVE_ESP32_DEVKIT1.SVP, MH-ET_LIVE_ESP32_DEVKIT1.IO13, MH-ET_LIVE_ESP32_DEVKIT1.IO22, MH-ET_LIVE_ESP32_DEVKIT1.IO16, MH-ET_LIVE_ESP32_DEVKIT1.IO4, MH-ET_LIVE_ESP32_DEVKIT1.IO2, M2.Pin_4, M1.Pin_4, R13.Pin_0, R13.Pin_1, C3.1, U7.GND, R17.Pin_0, C1.1, C1.2, R11.Pin_0, R11.Pin_1, S2.1, S2.2, R14.Pin_0, R14.Pin_1, C4.1, C4.2
  N3: U6.Din, U6.GND#3
  N4: U6.+5V#2, U7.K1-On
  N5: R16.Pin_1, J2.pin3
  VCC: Part2.VCC, Part1.HV, MH-ET_LIVE_ESP32_DEVKIT1.IO23, M2.Pin_3, U7.VCC
  N6: Part2.SDA, Part1.TX2_HV
  N7: Part2.SCL, Part1.RX2_HV
  N8: Part1.RX2_LV, MH-ET_LIVE_ESP32_DEVKIT1.IO14
  N9: Part1.LV, MH-ET_LIVE_ESP32_DEVKIT1.RST
  N10: Part1.RX_LV, MH-ET_LIVE_ESP32_DEVKIT1.TXD0
  N11: Part1.TX_LV, MH-ET_LIVE_ESP32_DEVKIT1.IO21
  N12: Part1.TX_HV, U7.IN1
  N13: J2.pin1, R17.Pin_1
  N14: J2.pin2, R15.Pin_1
  N15: R12.Pin_1, MH-ET_LIVE_ESP32_DEVKIT1.IO0, C3.2, R15.Pin_0
  N16: MH-ET_LIVE_ESP32_DEVKIT1.SD3, S2.3, S2.4
  N17: M1.Pin_3, U7.K1-In

custom parts:
  TXB0108 8-channel Bi-directional Logic Level Converter: Because the Arduino (and Basic Stamp) are 5V devices, and most modern sensors, displays, flash cards and modes are 3.3V-only, many makers find that they need to perform level shifting/conversion to protect the 3.3V device from 5V. Although one can use resistors to make a divider, for high speed transfers, the resistors can add a lot of slew and cause havoc that is tough to debug. For that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
  SK6812 RGBW LED Strip: SK6812 RGBW Strip
  LCD1602-I2C: A standard character display, usually with 2x16 characters. Comes in many colors with LCM1602 IIC attached.
  MH-ET LIVE ESP32 DEVKIT 38 pins: http://mh.nodebb.com/topic/2/mh-et-live-esp32-devkit
  2-Channel 5v Relay Shield: 2 Channel 5v Relay Shield w. 2x SPD-06VDC-SD-C
