# Fritzing sketch Car LED Controller3 (saved by Fritzing 0.9.10b)
circuit board: 9cm x 7cm
breadboards: 3

parts:
  Part1 = TXB0108 8-channel Bi-directional Logic Level Converter
  Part2 = TXB0108 8-channel Bi-directional Logic Level Converter
  J1 = shrouded pin header, 16 pins [form="♂ (shrouded male)"]
  Part3 = Logic Level Converter
  MH-ET_LIVE_ESP32_DEVKIT1 = MH-ET LIVE ESP32 DEVKIT 38 pins

nets:
  N1: Part1.VCCB, Part2.VCCA, Part3.HV
  N2: Part1.B1, J1.pin1
  N3: Part1.B2, J1.pin3
  N4: Part1.B3, J1.pin4
  N5: Part1.B4, J1.pin5
  N6: Part1.B5, J1.pin6
  N7: Part1.B6, J1.pin7
  GND: Part1.GND, Part1.OE, Part2.GND, Part2.OE, J1.pin2, J1.pin8, Part3.GND, MH-ET_LIVE_ESP32_DEVKIT1.GND
  N8: Part1.A6, MH-ET_LIVE_ESP32_DEVKIT1.IO4
  N9: Part1.A5, MH-ET_LIVE_ESP32_DEVKIT1.IO2
  N10: Part1.A4, MH-ET_LIVE_ESP32_DEVKIT1.IO15
  N11: Part1.A3, MH-ET_LIVE_ESP32_DEVKIT1.IO16
  N12: Part1.A2, MH-ET_LIVE_ESP32_DEVKIT1.IO17
  N13: Part1.A1, MH-ET_LIVE_ESP32_DEVKIT1.IO5
  N14: Part2.B1, J1.pin16
  N15: Part2.B2, J1.pin15
  N16: Part2.B3, J1.pin14
  N17: Part2.B4, J1.pin13
  N18: Part2.B5, J1.pin12
  N19: Part2.B6, J1.pin11
  N20: Part2.B7, J1.pin10
  N21: Part2.B8, J1.pin9
  N22: Part2.A8, MH-ET_LIVE_ESP32_DEVKIT1.IO32
  N23: Part2.A7, MH-ET_LIVE_ESP32_DEVKIT1.IO33
  N24: Part2.A6, MH-ET_LIVE_ESP32_DEVKIT1.IO25
  N25: Part2.A5, MH-ET_LIVE_ESP32_DEVKIT1.IO26
  N26: Part2.A4, MH-ET_LIVE_ESP32_DEVKIT1.IO27
  N27: Part2.A3, MH-ET_LIVE_ESP32_DEVKIT1.IO14
  N28: Part2.A2, MH-ET_LIVE_ESP32_DEVKIT1.IO12
  N29: Part2.A1, MH-ET_LIVE_ESP32_DEVKIT1.IO13
  N30: Part3.TX2_LV, MH-ET_LIVE_ESP32_DEVKIT1.IO23
  N31: Part3.RX2_LV, MH-ET_LIVE_ESP32_DEVKIT1.IO22
  N32: Part3.LV, MH-ET_LIVE_ESP32_DEVKIT1.3V3
  N33: Part3.RX_LV, MH-ET_LIVE_ESP32_DEVKIT1.IO21
  N34: Part3.TX_LV, MH-ET_LIVE_ESP32_DEVKIT1.IO18

custom parts:
  TXB0108 8-channel Bi-directional Logic Level Converter: Because the Arduino (and Basic Stamp) are 5V devices, and most modern sensors, displays, flash cards and modes are 3.3V-only, many makers find that they need to perform level shifting/conversion to protect the 3.3V device from 5V. Although one can use resistors to make a divider, for high speed transfers, the resistors can add a lot of slew and cause havoc that is tough to debug. For that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
  MH-ET LIVE ESP32 DEVKIT 38 pins: http://mh.nodebb.com/topic/2/mh-et-live-esp32-devkit
